// Logisim project PROJETO CD -TESTE.circ as structural Verilog: 8 circuits, main circuit FLIPFLOPD SUBIDA
module main (
  input  in_1,
  input  in_2,
  input  in_3
);

  wire button_1_out, button_2_out, button_3_out, button_4_out, clock_1_out;
  wire [3:0] \crônometro_1_c0 , \crônometro_1_c1 , \crônometro_1_c2 , \crônometro_1_c3 ,
       decodificador_1_inferior, decodificador_1_superior, decodificador_2_inferior,
       decodificador_2_superior, decodificador_3_inferior, decodificador_3_superior,
       decodificador_4_inferior, decodificador_4_superior;

  Clock clock_1 (.out(clock_1_out));
  \CRÔNOMETRO  \crônometro_1  (
    .ENABLE(in_1), .CLEAR(in_3), .CONF(clock_1_out), .C3(\crônometro_1_c3 ), .C2(\crônometro_1_c2 ),
    .C1(\crônometro_1_c1 ), .C0(\crônometro_1_c0 ), .in_1(button_3_out), .in_2(button_4_out),
    .in_3(button_1_out), .in_4(button_2_out));
  Button button_1 (.out(button_1_out));
  Button button_2 (.out(button_2_out));
  Button button_3 (.out(button_3_out));
  Button button_4 (.out(button_4_out));
  DECODIFICADOR decodificador_1 (
    .in_1(\crônometro_1_c3 ), .SUPERIOR(decodificador_1_superior), .INFERIOR(decodificador_1_inferior));
  _7_Segment_Display u_7_segment_display_1 (
    .g(decodificador_1_superior[3]), .f(decodificador_1_superior[2]), .a(decodificador_1_superior[1]),
    .b(decodificador_1_superior[0]), .e(decodificador_1_inferior[3]), .d(decodificador_1_inferior[2]),
    .c(decodificador_1_inferior[1]), .dp(decodificador_1_inferior[0]));
  DECODIFICADOR decodificador_2 (
    .in_1(\crônometro_1_c2 ), .SUPERIOR(decodificador_2_superior), .INFERIOR(decodificador_2_inferior));
  DECODIFICADOR decodificador_3 (
    .in_1(\crônometro_1_c1 ), .SUPERIOR(decodificador_3_superior), .INFERIOR(decodificador_3_inferior));
  _7_Segment_Display u_7_segment_display_2 (
    .g(decodificador_3_superior[3]), .f(decodificador_3_superior[2]), .a(decodificador_3_superior[1]),
    .b(decodificador_3_superior[0]), .e(decodificador_3_inferior[3]), .d(decodificador_3_inferior[2]),
    .c(decodificador_3_inferior[1]), .dp(decodificador_3_inferior[0]));
  _7_Segment_Display u_7_segment_display_3 (
    .g(decodificador_2_superior[3]), .f(decodificador_2_superior[2]), .a(decodificador_2_superior[1]),
    .b(decodificador_2_superior[0]), .e(decodificador_2_inferior[3]), .d(decodificador_2_inferior[2]),
    .c(decodificador_2_inferior[1]), .dp(decodificador_2_inferior[0]));
  DECODIFICADOR decodificador_4 (
    .in_1(\crônometro_1_c0 ), .SUPERIOR(decodificador_4_superior), .INFERIOR(decodificador_4_inferior));
  _7_Segment_Display u_7_segment_display_4 (
    .g(decodificador_4_superior[3]), .f(decodificador_4_superior[2]), .a(decodificador_4_superior[1]),
    .b(decodificador_4_superior[0]), .e(decodificador_4_inferior[3]), .d(decodificador_4_inferior[2]),
    .c(decodificador_4_inferior[1]), .dp(decodificador_4_inferior[0]));
endmodule

module FLIPFLOPD_SUBIDA (
  input  D,
  input  CLK,
  input  ENABLE,
  input  CLEAR,
  output Q
);

  wire and_1_out, and_2_out, and_3_out, nor_2_out, not_1_out, not_2_out, not_3_out, not_4_out, not_5_out;

  not not_1 (not_1_out, CLK);
  not not_2 (not_2_out, not_3_out);
  not not_3 (not_3_out, not_4_out);
  not not_4 (not_4_out, not_1_out);
  and and_1 (and_1_out, not_1_out, ENABLE, not_2_out);
  not not_5 (not_5_out, D);
  and and_2 (and_2_out, not_5_out, and_1_out);
  and and_3 (and_3_out, and_1_out, D);
  nor nor_1 (Q, and_2_out, CLEAR, nor_2_out);
  nor nor_2 (nor_2_out, Q, and_3_out);
endmodule

// 5-0
module CONTDEC (
  input  CONF,
  input  CLK,
  input  CLEAR,
  input  ENABLE,
  output [3:0] out_5,
  output out_6
);

  wire conversor05_1_q0, conversor05_1_q1, conversor05_1_q2, conversor05_1_q3, or_1_out;

  or or_1 (or_1_out, CONF, CLK);
  D_Flip_Flop #(.trigger("falling")) d_ff_1 (
    .clk(or_1_out), .D(conversor05_1_q0), .Q(out_5[3]), .en(ENABLE), .reset(CLEAR));  // open: Qn, preset
  D_Flip_Flop #(.trigger("falling")) d_ff_2 (
    .clk(or_1_out), .D(conversor05_1_q1), .Q(out_5[2]), .en(ENABLE), .reset(CLEAR));  // open: Qn, preset
  D_Flip_Flop #(.trigger("falling")) d_ff_3 (
    .clk(or_1_out), .D(conversor05_1_q2), .Q(out_5[1]), .en(ENABLE), .reset(CLEAR));  // open: Qn, preset
  Hex_Digit_Display hex_digit_display_1 (.value(out_5));  // open: dp
  CONVERSOR05 conversor05_1 (
    .D0(out_5[3]), .D1(out_5[2]), .D2(out_5[1]), .D3(out_5[0]), .Q0(conversor05_1_q0), .Q1(conversor05_1_q1),
    .Q2(conversor05_1_q2), .Q3(conversor05_1_q3), .SS(out_6));
  D_Flip_Flop #(.trigger("falling")) d_ff_4 (
    .clk(or_1_out), .D(conversor05_1_q3), .Q(out_5[0]), .en(ENABLE), .reset(CLEAR));  // open: Qn, preset
endmodule

// 9-0
module CONTUNI (
  input  CONF,
  input  CLK,
  input  CLEAR,
  input  ENABLE,
  output [3:0] out_5,
  output out_6
);

  wire conversor09_1_q0, conversor09_1_q1, conversor09_1_q2, conversor09_1_q3, or_1_out;

  or or_1 (or_1_out, CONF, CLK);
  D_Flip_Flop #(.trigger("falling")) d_ff_1 (
    .clk(or_1_out), .D(conversor09_1_q0), .Q(out_5[3]), .en(ENABLE), .reset(CLEAR));  // open: Qn, preset
  D_Flip_Flop #(.trigger("falling")) d_ff_2 (
    .clk(or_1_out), .D(conversor09_1_q1), .Q(out_5[2]), .en(ENABLE), .reset(CLEAR));  // open: Qn, preset
  D_Flip_Flop #(.trigger("falling")) d_ff_3 (
    .clk(or_1_out), .D(conversor09_1_q2), .Q(out_5[1]), .en(ENABLE), .reset(CLEAR));  // open: Qn, preset
  Hex_Digit_Display hex_digit_display_1 (.value(out_5));  // open: dp
  CONVERSOR09 conversor09_1 (
    .D0(out_5[3]), .D1(out_5[2]), .D2(out_5[1]), .D3(out_5[0]), .Q0(conversor09_1_q0), .Q1(conversor09_1_q1),
    .Q2(conversor09_1_q2), .Q3(conversor09_1_q3), .SS(out_6));
  D_Flip_Flop #(.trigger("falling")) d_ff_4 (
    .clk(or_1_out), .D(conversor09_1_q3), .Q(out_5[0]), .en(ENABLE), .reset(CLEAR));  // open: Qn, preset
endmodule

module CONVERSOR09 (
  input  D0,
  input  D1,
  input  D2,
  input  D3,
  output Q0,
  output Q1,
  output Q2,
  output Q3,
  output SS
);

  wire and_1_out, and_2_out, and_3_out, and_4_out, and_5_out, and_6_out, and_7_out, and_8_out, not_1_out,
       not_2_out, not_3_out, not_4_out, not_5_out, not_6_out, not_7_out, not_8_out, not_10_out, not_11_out,
       not_12_out, not_13_out;

  not not_1 (not_1_out, D0);
  not not_2 (not_2_out, D1);
  not not_3 (not_3_out, D2);
  not not_4 (not_4_out, D3);
  and and_1 (and_1_out, D1, D3);
  and and_2 (and_2_out, D1, D2);
  and and_3 (and_3_out, D0, not_5_out);
  not not_5 (not_5_out, D3);
  and and_4 (and_4_out, D2, D3);
  and and_5 (and_5_out, D1, not_6_out, not_7_out);
  not not_6 (not_6_out, D2);
  not not_7 (not_7_out, D3);
  and and_6 (and_6_out, D0, not_8_out);
  not not_8 (not_8_out, D3);
  not not_9 (Q3, D3);
  not not_10 (not_10_out, D0);
  not not_11 (not_11_out, D1);
  not not_12 (not_12_out, D2);
  not not_13 (not_13_out, D3);
  and and_7 (and_7_out, not_1_out, not_2_out, not_3_out, not_4_out);
  or or_1 (Q0, and_7_out, and_8_out);
  and and_8 (and_8_out, D0, D3);
  or or_2 (Q1, and_1_out, and_2_out, and_3_out);
  or or_3 (Q2, and_4_out, and_5_out, and_6_out);
  and and_9 (SS, not_10_out, not_11_out, not_12_out, not_13_out);
endmodule

module CONVERSOR05 (
  input  D0,
  input  D1,
  input  D2,
  input  D3,
  output Q0,
  output Q1,
  output Q2,
  output Q3,
  output SS
);

  wire and_2_out, and_3_out, and_4_out, and_5_out, and_6_out, and_7_out, and_8_out, and_9_out, and_10_out,
       and_11_out, and_12_out, not_1_out, not_2_out, not_3_out, not_4_out, not_5_out, not_6_out, not_7_out,
       not_8_out, not_9_out, not_10_out, not_11_out, not_12_out;

  and and_1 (Q0, D0, D1);
  not not_1 (not_1_out, D1);
  and and_2 (and_2_out, not_1_out, not_2_out, not_3_out);
  not not_2 (not_2_out, D2);
  not not_3 (not_3_out, D3);
  and and_3 (and_3_out, D1, D3);
  and and_4 (and_4_out, D1, D2);
  and and_5 (and_5_out, D0, not_4_out);
  not not_4 (not_4_out, D3);
  and and_6 (and_6_out, D2, D3);
  and and_7 (and_7_out, D1, not_5_out, not_6_out);
  not not_5 (not_5_out, D2);
  not not_6 (not_6_out, D3);
  and and_8 (and_8_out, D0, not_7_out);
  not not_7 (not_7_out, D3);
  and and_9 (and_9_out, D0, D1);
  not not_8 (not_8_out, D3);
  and and_10 (and_10_out, D0, D1);
  not not_9 (not_9_out, D0);
  not not_10 (not_10_out, D1);
  not not_11 (not_11_out, D2);
  not not_12 (not_12_out, D3);
  or or_1 (Q1, and_2_out, and_3_out, and_4_out, and_5_out);
  or or_2 (Q2, and_6_out, and_7_out, and_8_out, and_9_out);
  or or_3 (Q3, not_8_out, and_10_out);
  and and_11 (and_11_out, not_9_out, not_10_out, not_11_out, not_12_out);
  or or_4 (SS, and_11_out, and_12_out);
  and and_12 (and_12_out, D0, D1);
endmodule

module DECODIFICADOR (
  input  [3:0] in_1,
  output [3:0] SUPERIOR,
  output [3:0] INFERIOR
);

  wire and_1_out, and_2_out, and_3_out, and_4_out, and_5_out, and_6_out, and_7_out, and_8_out, and_9_out,
       and_10_out, and_11_out, and_12_out, and_13_out, and_14_out, and_15_out, and_16_out, and_17_out,
       and_18_out, and_19_out, and_20_out, and_21_out, and_22_out, and_23_out, nand_1_out, nor_1_out,
       nor_2_out, nor_3_out, nor_4_out, nor_5_out, or_1_out, or_2_out, or_3_out, or_4_out, or_5_out,
       or_6_out, or_7_out, or_8_out, xor_1_out, xor_2_out, xor_3_out;

  nor nor_1 (nor_1_out, in_1[3], in_1[2]);
  xor xor_1 (xor_1_out, in_1[2], in_1[0]);
  or or_1 (or_1_out, ~in_1[2], in_1[1]);  // OR_Gate
  or or_2 (or_2_out, in_1[2], in_1[1]);
  and and_1 (and_1_out, in_1[3], in_1[1]);
  and and_2 (and_2_out, in_1[3], ~in_1[2]);  // AND_Gate
  nor nor_2 (nor_2_out, in_1[1], in_1[0]);
  and and_3 (and_3_out, in_1[2], ~in_1[0]);  // AND_Gate
  and and_4 (and_4_out, ~in_1[1], in_1[2], ~in_1[3]);  // AND_Gate
  and and_5 (and_5_out, in_1[1], ~in_1[0]);  // AND_Gate
  and and_6 (and_6_out, in_1[3], ~in_1[2]);  // AND_Gate
  and and_7 (and_7_out, in_1[3], in_1[0]);
  and and_8 (and_8_out, ~in_1[3], in_1[2], ~in_1[1]);  // AND_Gate
  and and_9 (and_9_out, ~in_1[2], in_1[1], in_1[0]);  // AND_Gate
  or or_3 (or_3_out, in_1[2], in_1[1]);
  or or_4 (or_4_out, in_1[3], ~in_1[2]);  // OR_Gate
  or or_5 (or_5_out, ~in_1[3], in_1[2]);  // OR_Gate
  and and_10 (and_10_out, ~in_1[3], in_1[2], in_1[0]);  // AND_Gate
  and and_11 (and_11_out, in_1[3], ~in_1[2], ~in_1[1]);  // AND_Gate
  xor xor_2 (xor_2_out, in_1[3], in_1[1]);
  nand nand_1 (nand_1_out, in_1[3], in_1[0]);
  xor xor_3 (xor_3_out, in_1[3], in_1[2]);
  and and_12 (and_12_out, in_1[1], in_1[0]);
  nor nor_3 (nor_3_out, in_1[1], in_1[0]);
  and and_13 (and_13_out, in_1[2], in_1[0]);
  nor nor_4 (nor_4_out, in_1[2], in_1[0]);
  or or_6 (or_6_out, nor_1_out, xor_1_out);
  and and_14 (and_14_out, ~in_1[0], or_1_out);  // AND_Gate
  and and_15 (and_15_out, or_2_out, in_1[3]);
  and and_16 (and_16_out, or_4_out, ~in_1[0]);  // AND_Gate
  and and_17 (and_17_out, in_1[1], or_5_out);
  and and_18 (and_18_out, xor_2_out, in_1[0]);
  and and_19 (and_19_out, nand_1_out, ~in_1[2]);  // AND_Gate
  nor nor_5 (nor_5_out, in_1[3], in_1[1], in_1[0]);
  and and_20 (and_20_out, ~in_1[1], in_1[0]);  // AND_Gate
  or or_7 (or_7_out, and_12_out, nor_3_out);
  or or_8 (or_8_out, and_13_out, in_1[3], nor_4_out);
  and and_21 (and_21_out, or_8_out, ~in_1[1]);  // AND_Gate
  and and_22 (and_22_out, in_1[1], or_6_out);
  and and_23 (and_23_out, or_7_out, ~in_1[3]);  // AND_Gate
  or A (SUPERIOR[1], and_16_out, and_17_out, and_10_out, and_11_out);
  or B (SUPERIOR[0], and_18_out, and_19_out, nor_5_out);
  or C (INFERIOR[1], xor_3_out, and_20_out, and_23_out);
  or D (INFERIOR[2], and_21_out, and_22_out);
  or E (INFERIOR[3], and_14_out, and_15_out);
  or F (SUPERIOR[2], and_1_out, and_2_out, nor_2_out, and_3_out, and_4_out);
  or G (SUPERIOR[3], and_5_out, and_6_out, and_7_out, and_8_out, and_9_out);
  and and_24 (INFERIOR[0], in_1[3], or_3_out);

  // Notes on the sheet:
  //   W
  //   X
  //   Y
  //   Z
  //   ======================================================================
  //   ======================================================================
  //   ======================================================================
  //   ======================================================================
  //   ======================================================================
  //   ======================================================================
  //   ======================================================================
endmodule

module \CRÔNOMETRO  (
  input  in_1,
  input  in_2,
  input  in_3,
  input  in_4,
  input  ENABLE,
  input  CLEAR,
  input  CONF,
  output [3:0] C3,
  output [3:0] C2,
  output [3:0] C1,
  output [3:0] C0
);

  wire and_1_out, clock_1_out, contdec_2_out_6, contuni_1_out_6, contuni_2_out_6;

  Clock clock_1 (.out(clock_1_out));
  and and_1 (and_1_out, clock_1_out, ~CONF);  // AND_Gate
  Hex_Digit_Display hex_digit_display_1 (.value(C3));  // open: dp
  CONTDEC contdec_1 (.CLK(contuni_1_out_6), .CLEAR(CLEAR), .ENABLE(ENABLE), .out_5(C3), .CONF(in_1));  // open: out_6
  Hex_Digit_Display hex_digit_display_2 (.value(C2));  // open: dp
  CONTUNI contuni_1 (
    .out_6(contuni_1_out_6), .CLK(contdec_2_out_6), .CLEAR(CLEAR), .ENABLE(ENABLE), .out_5(C2), .CONF(in_2));
  Hex_Digit_Display hex_digit_display_3 (.value(C0));  // open: dp
  Hex_Digit_Display hex_digit_display_4 (.value(C1));  // open: dp
  CONTDEC contdec_2 (
    .out_6(contdec_2_out_6), .CLK(contuni_2_out_6), .CLEAR(CLEAR), .ENABLE(ENABLE), .out_5(C1), .CONF(in_3));
  CONTUNI contuni_2 (.out_6(contuni_2_out_6), .CLK(and_1_out), .CLEAR(CLEAR), .ENABLE(ENABLE), .out_5(C0), .CONF(in_4));
endmodule
