// Logisim project PROJETO.2 - CD.circ as structural Verilog
module main (
  input  in_1
);

  wire button_1_out, button_2_out, button_3_out, DMA_2_out, DMA_out, DSA_2_out, DSA_out, not_1_out,
       timer_ou_1_out_9, timer_ou_1_out_10, timer_ou_1_out_11, timer_ou_1_out_12, UMA_2_out, UMA_out,
       USA_2_out, USA_out;
  wire [3:0] \CRÔNOMETRO_2_c0 , \CRÔNOMETRO_2_c1 , \CRÔNOMETRO_2_c2 , \CRÔNOMETRO_2_c3 , \CRÔNOMETRO_c0 ,
       \CRÔNOMETRO_c1 , \CRÔNOMETRO_c2 , \CRÔNOMETRO_c3 , decodificador_1_inferior, decodificador_1_superior,
       decodificador_2_inferior, decodificador_2_superior, decodificador_3_inferior,
       decodificador_3_superior, decodificador_4_inferior, decodificador_4_superior,
       decodificador_5_inferior, decodificador_5_superior, decodificador_6_inferior,
       decodificador_6_superior, decodificador_7_inferior, decodificador_7_superior,
       decodificador_8_inferior, decodificador_8_superior;

  Button DSA (.out(DSA_out));
  Button DMA (.out(DMA_out));
  Button UMA (.out(UMA_out));
  \CRÔNOMETRO  \CRÔNOMETRO  (
    .ENABLE(button_3_out), .CLEAR(button_2_out), .CONF(button_1_out), .C3(\CRÔNOMETRO_c3 ),
    .C2(\CRÔNOMETRO_c2 ), .C1(\CRÔNOMETRO_c1 ), .C0(\CRÔNOMETRO_c0 ), .in_3(timer_ou_1_out_12),
    .in_1(timer_ou_1_out_11), .in_2(timer_ou_1_out_10), .in_4(timer_ou_1_out_9), .in_8(in_1));  // open: lig, Zer, Conf_2
  Button USA (.out(USA_out));
  TIMER_OU timer_ou_1 (
    .in_1(USA_out), .in_2(USA_2_out), .in_3(DSA_out), .in_4(DSA_2_out), .in_5(UMA_out), .in_6(UMA_2_out),
    .in_7(DMA_out), .in_8(DMA_2_out), .out_9(timer_ou_1_out_9), .out_10(timer_ou_1_out_10),
    .out_11(timer_ou_1_out_11), .out_12(timer_ou_1_out_12));
  Button UMA_2 (.out(UMA_2_out));
  Button DMA_2 (.out(DMA_2_out));
  \CRÔNOMETRO  \CRÔNOMETRO_2  (
    .ENABLE(button_3_out), .CLEAR(button_2_out), .CONF(button_1_out), .C3(\CRÔNOMETRO_2_c3 ),
    .C2(\CRÔNOMETRO_2_c2 ), .C1(\CRÔNOMETRO_2_c1 ), .C0(\CRÔNOMETRO_2_c0 ), .in_3(timer_ou_1_out_12),
    .in_1(timer_ou_1_out_11), .in_2(timer_ou_1_out_10), .in_4(timer_ou_1_out_9), .in_8(not_1_out));  // open: lig, Zer, Conf_2
  not not_1 (not_1_out, in_1);
  _7_Segment_Display u_7_segment_display_1 (
    .g(decodificador_1_superior[3]), .f(decodificador_1_superior[2]), .a(decodificador_1_superior[1]),
    .b(decodificador_1_superior[0]), .e(decodificador_1_inferior[3]), .d(decodificador_1_inferior[2]),
    .c(decodificador_1_inferior[1]), .dp(decodificador_1_inferior[0]));
  Button DSA_2 (.out(DSA_2_out));
  Button USA_2 (.out(USA_2_out));
  DECODIFICADOR decodificador_1 (
    .in_1(\CRÔNOMETRO_2_c3 ), .SUPERIOR(decodificador_1_superior), .INFERIOR(decodificador_1_inferior));
  DECODIFICADOR decodificador_2 (
    .in_1(\CRÔNOMETRO_2_c2 ), .SUPERIOR(decodificador_2_superior), .INFERIOR(decodificador_2_inferior));
  _7_Segment_Display u_7_segment_display_2 (
    .g(decodificador_2_superior[3]), .f(decodificador_2_superior[2]), .a(decodificador_2_superior[1]),
    .b(decodificador_2_superior[0]), .e(decodificador_2_inferior[3]), .d(decodificador_2_inferior[2]),
    .c(decodificador_2_inferior[1]), .dp(decodificador_2_inferior[0]));
  DECODIFICADOR decodificador_3 (
    .in_1(\CRÔNOMETRO_2_c1 ), .SUPERIOR(decodificador_3_superior), .INFERIOR(decodificador_3_inferior));
  _7_Segment_Display u_7_segment_display_3 (
    .g(decodificador_3_superior[3]), .f(decodificador_3_superior[2]), .a(decodificador_3_superior[1]),
    .b(decodificador_3_superior[0]), .e(decodificador_3_inferior[3]), .d(decodificador_3_inferior[2]),
    .c(decodificador_3_inferior[1]), .dp(decodificador_3_inferior[0]));
  LED led_1 (.in(1'b1));
  LED led_2 (.in(1'b1));
  DECODIFICADOR decodificador_4 (
    .in_1(\CRÔNOMETRO_2_c0 ), .SUPERIOR(decodificador_4_superior), .INFERIOR(decodificador_4_inferior));
  _7_Segment_Display u_7_segment_display_4 (
    .g(decodificador_4_superior[3]), .f(decodificador_4_superior[2]), .a(decodificador_4_superior[1]),
    .b(decodificador_4_superior[0]), .e(decodificador_4_inferior[3]), .d(decodificador_4_inferior[2]),
    .c(decodificador_4_inferior[1]), .dp(decodificador_4_inferior[0]));
  Button button_1 (.out(button_1_out));
  DECODIFICADOR decodificador_5 (
    .in_1(\CRÔNOMETRO_c3 ), .SUPERIOR(decodificador_5_superior), .INFERIOR(decodificador_5_inferior));
  _7_Segment_Display u_7_segment_display_5 (
    .g(decodificador_5_superior[3]), .f(decodificador_5_superior[2]), .a(decodificador_5_superior[1]),
    .b(decodificador_5_superior[0]), .e(decodificador_5_inferior[3]), .d(decodificador_5_inferior[2]),
    .c(decodificador_5_inferior[1]), .dp(decodificador_5_inferior[0]));
  Button button_2 (.out(button_2_out));
  Button button_3 (.out(button_3_out));
  DECODIFICADOR decodificador_6 (
    .in_1(\CRÔNOMETRO_c2 ), .SUPERIOR(decodificador_6_superior), .INFERIOR(decodificador_6_inferior));
  _7_Segment_Display u_7_segment_display_6 (
    .g(decodificador_6_superior[3]), .f(decodificador_6_superior[2]), .a(decodificador_6_superior[1]),
    .b(decodificador_6_superior[0]), .e(decodificador_6_inferior[3]), .d(decodificador_6_inferior[2]),
    .c(decodificador_6_inferior[1]), .dp(decodificador_6_inferior[0]));
  LED led_3 (.in(1'b1));
  LED led_4 (.in(1'b1));
  DECODIFICADOR decodificador_7 (
    .in_1(\CRÔNOMETRO_c1 ), .SUPERIOR(decodificador_7_superior), .INFERIOR(decodificador_7_inferior));
  _7_Segment_Display u_7_segment_display_7 (
    .g(decodificador_8_superior[3]), .f(decodificador_8_superior[2]), .a(decodificador_8_superior[1]),
    .b(decodificador_8_superior[0]), .e(decodificador_8_inferior[3]), .d(decodificador_8_inferior[2]),
    .c(decodificador_8_inferior[1]), .dp(decodificador_8_inferior[0]));
  _7_Segment_Display u_7_segment_display_8 (
    .g(decodificador_7_superior[3]), .f(decodificador_7_superior[2]), .a(decodificador_7_superior[1]),
    .b(decodificador_7_superior[0]), .e(decodificador_7_inferior[3]), .d(decodificador_7_inferior[2]),
    .c(decodificador_7_inferior[1]), .dp(decodificador_7_inferior[0]));
  DECODIFICADOR decodificador_8 (
    .in_1(\CRÔNOMETRO_c0 ), .SUPERIOR(decodificador_8_superior), .INFERIOR(decodificador_8_inferior));
endmodule

// 5-0
module CONTDEC (
  input  CLKBTN,
  input  CONF,
  input  CLK,
  input  CLEAR,
  input  ENABLE,
  output [3:0] out_6,
  output out_7,
  output out_8
);

  wire and_1_out, and_2_out, b_1_q0, b_1_q1, b_1_q2, b_1_q3, or_1_out;

  and and_1 (and_1_out, CLKBTN, CONF);
  and and_2 (and_2_out, CLK, ~CONF);  // AND_Gate
  or or_1 (or_1_out, and_1_out, and_2_out);
  D_Flip_Flop d_ff_1 (.clk(or_1_out), .D(b_1_q0), .Q(out_6[3]), .en(ENABLE), .reset(CLEAR));  // open: Qn, preset
  D_Flip_Flop d_ff_2 (.clk(or_1_out), .D(b_1_q1), .Q(out_6[2]), .en(ENABLE), .reset(CLEAR));  // open: Qn, preset
  B b_1 (
    .D0(out_6[3]), .D1(out_6[2]), .D2(out_6[1]), .D3(out_6[0]), .Q0(b_1_q0), .Q1(b_1_q1), .Q2(b_1_q2),
    .Q3(b_1_q3), .SS(out_8), .zz(out_7));
  D_Flip_Flop d_ff_3 (.clk(or_1_out), .D(b_1_q2), .Q(out_6[1]), .en(ENABLE), .reset(CLEAR));  // open: Qn, preset
  Hex_Digit_Display hex_digit_display_1 (.value(out_6));  // open: dp
  D_Flip_Flop d_ff_4 (.clk(or_1_out), .D(b_1_q3), .Q(out_6[0]), .en(ENABLE), .reset(CLEAR));  // open: Qn, preset
endmodule

// 9-0
module CONTUNI (
  input  CLKBTN,
  input  CONF,
  input  CLK,
  input  CLEAR,
  input  ENABLE,
  output [3:0] out_6,
  output out_7,
  output out_8
);

  wire a_1_q0, a_1_q1, a_1_q2, a_1_q3, and_1_out, and_2_out, or_1_out;

  and and_1 (and_1_out, CLKBTN, CONF);
  and and_2 (and_2_out, CLK, ~CONF);  // AND_Gate
  or or_1 (or_1_out, and_1_out, and_2_out);
  D_Flip_Flop d_ff_1 (.clk(or_1_out), .D(a_1_q0), .Q(out_6[3]), .en(ENABLE), .reset(CLEAR));  // open: Qn, preset
  D_Flip_Flop d_ff_2 (.clk(or_1_out), .D(a_1_q1), .Q(out_6[2]), .en(ENABLE), .reset(CLEAR));  // open: Qn, preset
  A a_1 (
    .D0(out_6[3]), .D1(out_6[2]), .D2(out_6[1]), .D3(out_6[0]), .Q0(a_1_q0), .Q1(a_1_q1), .Q2(a_1_q2),
    .Q3(a_1_q3), .SS(out_8), .zz(out_7));
  D_Flip_Flop d_ff_3 (.clk(or_1_out), .D(a_1_q2), .Q(out_6[1]), .en(ENABLE), .reset(CLEAR));  // open: Qn, preset
  Hex_Digit_Display hex_digit_display_1 (.value(out_6));  // open: dp
  D_Flip_Flop d_ff_4 (.clk(or_1_out), .D(a_1_q3), .Q(out_6[0]), .en(ENABLE), .reset(CLEAR));  // open: Qn, preset
endmodule

module DECODIFICADOR (
  input  [3:0] in_1,
  output [3:0] SUPERIOR,
  output [3:0] INFERIOR
);

  wire and_1_out, and_2_out, and_3_out, and_4_out, and_5_out, and_6_out, and_7_out, and_8_out, and_9_out,
       and_10_out, and_11_out, and_12_out, and_13_out, and_14_out, and_15_out, and_16_out, and_17_out,
       and_18_out, and_19_out, and_20_out, and_22_out, and_23_out, and_24_out, nand_1_out, nor_1_out,
       nor_2_out, nor_3_out, nor_4_out, nor_5_out, or_1_out, or_2_out, or_3_out, or_4_out, or_5_out,
       or_6_out, or_7_out, or_8_out, xor_1_out, xor_2_out, xor_3_out;

  or or_1 (or_1_out, in_1[3], ~in_1[2]);  // OR_Gate
  or or_2 (or_2_out, ~in_1[3], in_1[2]);  // OR_Gate
  and and_1 (and_1_out, ~in_1[3], in_1[2], in_1[0]);  // AND_Gate
  and and_2 (and_2_out, in_1[3], ~in_1[2], ~in_1[1]);  // AND_Gate
  xor xor_1 (xor_1_out, in_1[3], in_1[1]);
  nand nand_1 (nand_1_out, in_1[3], in_1[0]);
  nor nor_1 (nor_1_out, in_1[3], in_1[1], in_1[0]);
  and and_3 (and_3_out, ~in_1[1], in_1[0]);  // AND_Gate
  xor xor_2 (xor_2_out, in_1[3], in_1[2]);
  and and_4 (and_4_out, in_1[1], in_1[0]);
  nor nor_2 (nor_2_out, in_1[1], in_1[0]);
  and and_5 (and_5_out, in_1[2], in_1[0]);
  nor nor_3 (nor_3_out, in_1[2], in_1[0]);
  nor nor_4 (nor_4_out, in_1[3], in_1[2]);
  xor xor_3 (xor_3_out, in_1[2], in_1[0]);
  or or_3 (or_3_out, ~in_1[2], in_1[1]);  // OR_Gate
  or or_4 (or_4_out, in_1[2], in_1[1]);
  and and_6 (and_6_out, in_1[3], in_1[1]);
  and and_7 (and_7_out, in_1[3], ~in_1[2]);  // AND_Gate
  nor nor_5 (nor_5_out, in_1[1], in_1[0]);
  and and_8 (and_8_out, in_1[2], ~in_1[0]);  // AND_Gate
  and and_9 (and_9_out, ~in_1[1], in_1[2], ~in_1[3]);  // AND_Gate
  and and_10 (and_10_out, in_1[1], ~in_1[0]);  // AND_Gate
  and and_11 (and_11_out, in_1[3], ~in_1[2]);  // AND_Gate
  and and_12 (and_12_out, in_1[3], in_1[0]);
  and and_13 (and_13_out, ~in_1[3], in_1[2], ~in_1[1]);  // AND_Gate
  and and_14 (and_14_out, ~in_1[2], in_1[1], in_1[0]);  // AND_Gate
  or or_5 (or_5_out, in_1[2], in_1[1]);
  and and_15 (and_15_out, or_1_out, ~in_1[0]);  // AND_Gate
  and and_16 (and_16_out, in_1[1], or_2_out);
  and and_17 (and_17_out, xor_1_out, in_1[0]);
  and and_18 (and_18_out, nand_1_out, ~in_1[2]);  // AND_Gate
  or or_6 (or_6_out, and_4_out, nor_2_out);
  or or_7 (or_7_out, and_5_out, in_1[3], nor_3_out);
  or or_8 (or_8_out, nor_4_out, xor_3_out);
  and and_19 (and_19_out, ~in_1[0], or_3_out);  // AND_Gate
  or E (INFERIOR[3], and_19_out, and_20_out);
  and and_20 (and_20_out, or_4_out, in_1[3]);
  or F (SUPERIOR[2], and_6_out, and_7_out, nor_5_out, and_8_out, and_9_out);
  or G (SUPERIOR[3], and_10_out, and_11_out, and_12_out, and_13_out, and_14_out);
  and and_21 (INFERIOR[0], in_1[3], or_5_out);
  or A (SUPERIOR[1], and_15_out, and_16_out, and_1_out, and_2_out);
  or B (SUPERIOR[0], and_17_out, and_18_out, nor_1_out);
  or C (INFERIOR[1], and_3_out, xor_2_out, and_22_out);
  and and_22 (and_22_out, or_6_out, ~in_1[3]);  // AND_Gate
  and and_23 (and_23_out, or_7_out, ~in_1[1]);  // AND_Gate
  or D (INFERIOR[2], and_23_out, and_24_out);
  and and_24 (and_24_out, in_1[1], or_8_out);
endmodule

module \CRÔNOMETRO  (
  input  in_1,
  input  in_2,
  input  in_3,
  input  in_4,
  input  ENABLE,
  input  CLEAR,
  input  CONF,
  input  in_8,
  output [3:0] C3,
  output [3:0] C2,
  output [3:0] C1,
  output [3:0] C0,
  output Zer,
  output lig,
  output Conf_2
);

  wire and_1_out, clock_1_out, contdec_1_out_7, contdec_2_out_7, contdec_2_out_8, contuni_1_out_7,
       contuni_1_out_8, contuni_2_out_7, contuni_2_out_8;

  \BOTÃO  \botão_1  (.PROXIMO(ENABLE), .Q0(lig));  // open: CLK, Q1
  Clock clock_1 (.out(clock_1_out));
  Hex_Digit_Display hex_digit_display_1 (.value(C3));  // open: dp
  and and_1 (and_1_out, lig, ~Zer, clock_1_out, in_8);  // AND_Gate
  \BOTÃO  \botão_2  (.PROXIMO(CONF), .Q0(Conf_2));  // open: CLK, Q1
  Hex_Digit_Display hex_digit_display_2 (.value(C2));  // open: dp
  CONTDEC contdec_1 (
    .CLK(contuni_1_out_8), .CLEAR(CLEAR), .ENABLE(lig), .out_6(C3), .out_7(contdec_1_out_7), .CLKBTN(in_3),
    .CONF(Conf_2));  // open: out_8
  Hex_Digit_Display hex_digit_display_3 (.value(C1));  // open: dp
  CONTDEC contdec_2 (
    .out_8(contdec_2_out_8), .CLK(contuni_2_out_8), .CLEAR(CLEAR), .ENABLE(lig), .out_6(C1),
    .out_7(contdec_2_out_7), .CLKBTN(in_2), .CONF(Conf_2));
  CONTUNI contuni_1 (
    .out_8(contuni_1_out_8), .CLK(contdec_2_out_8), .CLEAR(CLEAR), .ENABLE(lig), .out_6(C2),
    .out_7(contuni_1_out_7), .CLKBTN(in_1), .CONF(Conf_2));
  Hex_Digit_Display hex_digit_display_4 (.value(C0));  // open: dp
  CONTUNI contuni_2 (
    .out_8(contuni_2_out_8), .CLK(and_1_out), .CLEAR(CLEAR), .ENABLE(lig), .out_6(C0),
    .out_7(contuni_2_out_7), .CLKBTN(in_4), .CONF(Conf_2));
  and and_2 (Zer, contuni_2_out_7, contdec_2_out_7, contuni_1_out_7, contdec_1_out_7);
endmodule

module CORE (
  input  PROXIMO,
  input  CHUTE,
  input  CLEAR,
  input  ENABLE,
  input  [3:0] in_5,
  output [3:0] out_6,
  output [3:0] out_7
);

  wire and_1_out, and_2_out, and_3_out, and_4_out, and_5_out, and_6_out, multiplexador_sml_1_out_3,
       multiplexador_sml_1_out_4, or_1_out, passarchute_1_out_8, passarchute_1_out_9, somador_1_out_4,
       somador_2_out_4, troca_1_out_2, verificador_1_out_4, verificador_1_out_5, verificador_1_out_6,
       verificador_1_out_7;
  wire [2:0] comparador_1_out_4, comparador_2_out_4, comparador_5b_1_out_4;
  wire [3:0] decodificador_1_inferior, decodificador_1_superior, decodificador_2_inferior,
       decodificador_2_superior, decodificador_3_inferior, decodificador_3_superior, passarchute_1_out_6,
       passarchute_1_out_7, visor_negado_1_q3, visor_negado_2_q3, visor_negado_3_q3, X_out_5, Y_out_5;
  wire [4:0] somador_1_out_3, somador_2_out_3;

  VISOR_NEGADO visor_negado_1 (
    .D0(in_5[3]), .D1(in_5[2]), .D2(in_5[1]), .D3(in_5[0]), .Q0(visor_negado_1_q3[3]),
    .Q1(visor_negado_1_q3[2]), .Q2(visor_negado_1_q3[1]), .Q3(visor_negado_1_q3[0]));
  VERIFICADOR verificador_1 (
    .ENABLE(ENABLE), .CLEAR(CLEAR), .PROX(PROXIMO), .out_4(verificador_1_out_4), .out_5(verificador_1_out_5),
    .out_6(verificador_1_out_6), .out_7(verificador_1_out_7));
  _7_Segment_Display u_7_segment_display_1 (.g(in_5[3]));  // open: f, a, b, e, d, c, dp
  DECODIFICADOR decodificador_1 (
    .in_1(visor_negado_1_q3), .SUPERIOR(decodificador_1_superior), .INFERIOR(decodificador_1_inferior));
  _7_Segment_Display u_7_segment_display_2 (
    .g(decodificador_1_superior[3]), .f(decodificador_1_superior[2]), .a(decodificador_1_superior[1]),
    .b(decodificador_1_superior[0]), .e(decodificador_1_inferior[3]), .d(decodificador_1_inferior[2]),
    .c(decodificador_1_inferior[1]), .dp(decodificador_1_inferior[0]));
  and and_1 (and_1_out, CHUTE, verificador_1_out_4);
  \VARIÁVEL  X (.in_1(in_5), .CLK(and_1_out), .CLEAR(CLEAR), .ENABLE(ENABLE), .out_5(X_out_5));
  and and_2 (and_2_out, CHUTE, verificador_1_out_5);
  VISOR_NEGADO visor_negado_2 (
    .D0(Y_out_5[3]), .D1(Y_out_5[2]), .D2(Y_out_5[1]), .D3(Y_out_5[0]), .Q0(visor_negado_2_q3[3]),
    .Q1(visor_negado_2_q3[2]), .Q2(visor_negado_2_q3[1]), .Q3(visor_negado_2_q3[0]));
  VISOR_NEGADO visor_negado_3 (
    .D0(X_out_5[3]), .D1(X_out_5[2]), .D2(X_out_5[1]), .D3(X_out_5[0]), .Q0(visor_negado_3_q3[3]),
    .Q1(visor_negado_3_q3[2]), .Q2(visor_negado_3_q3[1]), .Q3(visor_negado_3_q3[0]));
  \VARIÁVEL  Y (.in_1(in_5), .CLK(and_2_out), .CLEAR(CLEAR), .ENABLE(ENABLE), .out_5(Y_out_5));
  _7_Segment_Display u_7_segment_display_3 (.g(Y_out_5[3]));  // open: f, a, b, e, d, c, dp
  DECODIFICADOR decodificador_2 (
    .in_1(visor_negado_2_q3), .SUPERIOR(decodificador_2_superior), .INFERIOR(decodificador_2_inferior));
  _7_Segment_Display u_7_segment_display_4 (.g(X_out_5[3]));  // open: f, a, b, e, d, c, dp
  DECODIFICADOR decodificador_3 (
    .in_1(visor_negado_3_q3), .SUPERIOR(decodificador_3_superior), .INFERIOR(decodificador_3_inferior));
  COMPARADOR comparador_1 (
    .CHUTE(passarchute_1_out_6), .in_3(4'b0100), .NEG(passarchute_1_out_8), .out_4(comparador_1_out_4));
  passarChute passarchute_1 (
    .ENABLE(ENABLE), .CLK(verificador_1_out_6), .CLEAR(CLEAR), .in_4(X_out_5), .in_5(Y_out_5),
    .out_6(passarchute_1_out_6), .out_7(passarchute_1_out_7), .out_8(passarchute_1_out_8),
    .out_9(passarchute_1_out_9));
  _7_Segment_Display u_7_segment_display_5 (
    .g(decodificador_2_superior[3]), .f(decodificador_2_superior[2]), .a(decodificador_2_superior[1]),
    .b(decodificador_2_superior[0]), .e(decodificador_2_inferior[3]), .d(decodificador_2_inferior[2]),
    .c(decodificador_2_inferior[1]), .dp(decodificador_2_inferior[0]));
  _7_Segment_Display u_7_segment_display_6 (
    .g(decodificador_3_superior[3]), .f(decodificador_3_superior[2]), .a(decodificador_3_superior[1]),
    .b(decodificador_3_superior[0]), .e(decodificador_3_inferior[3]), .d(decodificador_3_inferior[2]),
    .c(decodificador_3_inferior[1]), .dp(decodificador_3_inferior[0]));
  COMPARADOR comparador_2 (
    .CHUTE(passarchute_1_out_7), .in_3(4'b0100), .NEG(passarchute_1_out_9), .out_4(comparador_2_out_4));
  TROCA troca_1 (.in_1(verificador_1_out_7), .out_2(troca_1_out_2));
  and and_3 (and_3_out, comparador_2_out_4[1], comparador_1_out_4[1]);
  MULTIPLEXADOR_SML multiplexador_sml_1 (
    .in_2(and_3_out), .JOGADOR(troca_1_out_2), .out_3(multiplexador_sml_1_out_3),
    .out_4(multiplexador_sml_1_out_4));
  SOMADOR somador_1 (
    .in_1(passarchute_1_out_6), .in_2(passarchute_1_out_7), .out_3(somador_1_out_3), .out_4(somador_1_out_4));
  or or_1 (or_1_out, somador_1_out_4, somador_2_out_4);
  SOMADOR somador_2 (.in_1(4'b0100), .in_2(4'b0100), .out_3(somador_2_out_3), .out_4(somador_2_out_4));
  PONTO PONTo_A (.CLK(verificador_1_out_6), .CLEAR(CLEAR), .ENABLE(multiplexador_sml_1_out_3), .out_4(out_6));
  COMPARADOR_5B comparador_5b_1 (
    .CHUTE(somador_1_out_3), .in_2(or_1_out), .in_3(somador_2_out_3), .out_4(comparador_5b_1_out_4));
  PONTO PONTO_B (.CLK(verificador_1_out_6), .CLEAR(CLEAR), .ENABLE(multiplexador_sml_1_out_4), .out_4(out_7));
  and and_4 (and_4_out, verificador_1_out_6, comparador_5b_1_out_4[0]);
  and and_5 (and_5_out, verificador_1_out_6, comparador_5b_1_out_4[1]);
  LED led_1 (.in(and_4_out));
  LED led_2 (.in(and_5_out));
  and and_6 (and_6_out, verificador_1_out_6, comparador_5b_1_out_4[2]);
  LED led_3 (.in(and_6_out));
endmodule

module NEGADOR (
  input  [3:0] in_1,
  input  [3:0] in_2,
  input  in_3,
  output [3:0] out_4,
  output [3:0] out_5
);

  wire not_1_out;

  not not_1 (not_1_out, in_3);
  NEGA nega_1 (
    .D0(in_1[0]), .D1(in_1[1]), .D2(in_1[2]), .D3(in_1[3]), .D4(not_1_out), .Q0(out_4[0]), .Q1(out_4[1]),
    .Q2(out_4[2]), .Q3(out_4[3]));
  NEGA nega_2 (
    .D0(in_2[0]), .D1(in_2[1]), .D2(in_2[2]), .D3(in_2[3]), .D4(in_3), .Q0(out_5[0]), .Q1(out_5[1]),
    .Q2(out_5[2]), .Q3(out_5[3]));
endmodule

// COMP
module COMPARADOR (
  input  [3:0] CHUTE,
  input  NEG,
  input  [3:0] in_3,
  output [2:0] out_4
);

  wire _0_2_out, _0_out, _1_2_out, _1_out, _2_2_out, _2_out, _3_2_out, _3_out, MAIOR_out, MENOR_out;

  xnor _0 (_0_out, in_3[0], CHUTE[0]);
  xnor _1 (_1_out, in_3[1], CHUTE[1]);
  xnor _2 (_2_out, in_3[2], CHUTE[2]);
  xnor _3 (_3_out, in_3[3], CHUTE[3]);
  and IGUAL (out_4[1], _0_out, _1_out, _2_out, _3_out);
  and _0_2 (_0_2_out, CHUTE[0], _1_out, _2_out, _3_out, ~in_3[0]);  // AND_Gate
  and _1_2 (_1_2_out, CHUTE[1], ~in_3[1], _2_out, _3_out);  // AND_Gate
  and _2_2 (_2_2_out, CHUTE[2], ~in_3[2], _3_out);  // AND_Gate
  and _3_2 (_3_2_out, CHUTE[3], ~in_3[3]);  // AND_Gate
  or MAIOR (MAIOR_out, _0_2_out, _1_2_out, _2_2_out, _3_2_out);
  nor MENOR (MENOR_out, out_4[1], MAIOR_out);
  xor xor_1 (out_4[0], NEG, MENOR_out);
  xor xor_2 (out_4[2], NEG, MAIOR_out);
endmodule

module SUM (
  input  in_1,
  input  in_2,
  input  in_3,
  output SUM,
  output CARRY
);

  wire AND_2_out, AND_3_out, AND_out, xor_1_out;

  xor xor_1 (xor_1_out, in_1, in_2);
  xor xor_2 (SUM, xor_1_out, in_3);
  and AND (AND_out, in_1, in_2);
  and AND_2 (AND_2_out, in_1, in_3);
  and AND_3 (AND_3_out, in_2, in_3);
  or or_1 (CARRY, AND_out, AND_2_out, AND_3_out);
endmodule

// SOMA
module SOMADOR (
  input  [3:0] in_1,
  input  [3:0] in_2,
  output [4:0] out_3,
  output out_4
);

  wire and_1_out, and_2_out, sum_1_carry, sum_2_carry, sum_3_carry;
  wire [2:0] comparador_1_out_4, comparador_2_out_4;

  COMPARADOR comparador_1 (.CHUTE(in_2), .in_3(in_1), .NEG(in_1[3]), .out_4(comparador_1_out_4));
  COMPARADOR comparador_2 (.CHUTE(in_1), .in_3(in_2), .NEG(in_2[3]), .out_4(comparador_2_out_4));
  SUM sum_1 (.in_1(1'b0), .in_2(in_1[0]), .in_3(in_2[0]), .SUM(out_3[0]), .CARRY(sum_1_carry));
  SUM sum_2 (.in_1(sum_1_carry), .in_2(in_1[1]), .in_3(in_2[1]), .SUM(out_3[1]), .CARRY(sum_2_carry));
  SUM sum_3 (.in_1(sum_2_carry), .in_2(in_1[2]), .in_3(in_2[2]), .SUM(out_3[2]), .CARRY(sum_3_carry));
  SUM sum_4 (.in_1(sum_3_carry), .in_2(in_1[3]), .in_3(in_2[3]), .SUM(out_3[3]), .CARRY(out_3[4]));
  and and_1 (and_1_out, in_1[3], comparador_1_out_4[2]);
  and and_2 (and_2_out, in_2[3], comparador_2_out_4[2]);
  or or_1 (out_4, and_1_out, and_2_out);
endmodule

module \VARIÁVEL  (
  input  [3:0] in_1,
  input  CLK,
  input  CLEAR,
  input  ENABLE,
  output [3:0] out_5
);

  D_Flip_Flop d_ff_1 (.clk(CLK), .D(in_1[3]), .Q(out_5[3]), .en(ENABLE), .reset(CLEAR));  // open: Qn, preset
  D_Flip_Flop d_ff_2 (.clk(CLK), .D(in_1[2]), .Q(out_5[2]), .en(ENABLE), .reset(CLEAR));  // open: Qn, preset
  D_Flip_Flop d_ff_3 (.clk(CLK), .D(in_1[1]), .Q(out_5[1]), .en(ENABLE), .reset(CLEAR));  // open: Qn, preset
  D_Flip_Flop d_ff_4 (.clk(CLK), .D(in_1[0]), .Q(out_5[0]), .en(ENABLE), .reset(CLEAR));  // open: Qn, preset
  Hex_Digit_Display hex_digit_display_1 (.value(out_5));  // open: dp
endmodule

module passarChute (
  input  ENABLE,
  input  CLK,
  input  CLEAR,
  input  [3:0] in_4,
  input  [3:0] in_5,
  output [3:0] out_6,
  output [3:0] out_7,
  output out_8,
  output out_9
);

  \VARIÁVEL  \variável_1  (.in_1(in_4), .CLK(CLK), .CLEAR(CLEAR), .ENABLE(ENABLE), .out_5(out_6));
  \VARIÁVEL  \variável_2  (.in_1(in_5), .CLK(CLK), .CLEAR(CLEAR), .ENABLE(ENABLE), .out_5(out_7));

  assign out_8 = in_5[3];
  assign out_9 = in_4[3];
endmodule

module \BOTÃO  (
  input  PROXIMO,
  output CLK,
  output Q0,
  output Q1
);

  wire not_1_out;

  not not_1 (not_1_out, Q0);
  D_Flip_Flop d_ff_1 (.clk(PROXIMO), .D(not_1_out), .Q(Q0));  // open: Qn, preset, en, reset
  not not_2 (Q1, Q0);

  assign CLK = PROXIMO;
endmodule

module FLIPFLOPD_DESCIDA (
  input  D,
  input  CLK,
  input  ENABLE,
  input  CLEAR,
  output Q
);

  wire and_1_out, and_2_out, and_3_out, nor_2_out, not_1_out, not_2_out, not_3_out, not_4_out, not_5_out;

  not not_1 (not_1_out, CLK);
  not not_2 (not_2_out, not_3_out);
  not not_3 (not_3_out, not_4_out);
  not not_4 (not_4_out, not_1_out);
  not not_5 (not_5_out, D);
  and and_1 (and_1_out, not_1_out, ENABLE, not_2_out);
  and and_2 (and_2_out, not_5_out, and_1_out);
  nor nor_1 (Q, and_2_out, CLEAR, nor_2_out);
  nor nor_2 (nor_2_out, Q, and_3_out);
  and and_3 (and_3_out, and_1_out, D);
endmodule

module SUBTRATOR (
  input  [3:0] in_1,
  input  [3:0] in_2,
  output [4:0] out_3
);

  wire [4:4] somador_1_out_3;

  SOMADOR somador_1 (.in_1(in_1), .in_2(in_2), .out_3({somador_1_out_3[4], out_3[3:0]}));  // open: out_4

  assign out_3[4] = 1'b0;
endmodule

module NEG (
  input  D0,
  input  D1,
  input  D2,
  input  D3,
  input  D4,
  output Q0,
  output Q1,
  output Q2,
  output Q3,
  output Q4
);

  wire and_1_out, and_2_out, and_3_out, and_4_out, and_5_out, and_6_out, and_7_out, and_8_out, and_9_out,
       and_10_out, and_11_out, and_12_out, not_1_out, not_2_out, not_3_out, not_4_out, not_5_out, not_6_out,
       not_7_out, not_8_out, not_9_out, not_10_out, not_11_out, not_12_out, not_13_out, not_14_out,
       not_15_out;

  not not_1 (not_1_out, D0);
  not not_2 (not_2_out, D0);
  not not_3 (not_3_out, D0);
  not not_4 (not_4_out, D1);
  not not_5 (not_5_out, D2);
  not not_6 (not_6_out, D3);
  not not_7 (not_7_out, D4);
  not not_8 (not_8_out, D1);
  not not_9 (not_9_out, D1);
  not not_10 (not_10_out, D2);
  not not_11 (not_11_out, D3);
  not not_12 (not_12_out, D4);
  not not_13 (not_13_out, D2);
  not not_14 (not_14_out, D3);
  not not_15 (not_15_out, D4);
  and and_1 (and_1_out, not_1_out, D3, D4);
  and and_2 (and_2_out, not_2_out, D2, D4);
  and and_3 (and_3_out, not_3_out, D1, D4);
  and and_4 (and_4_out, D0, not_4_out, not_5_out, not_6_out);
  and and_5 (and_5_out, D0, not_7_out);
  and and_6 (and_6_out, not_8_out, D3, D4);
  and and_7 (and_7_out, not_9_out, D2, D4);
  and and_8 (and_8_out, D1, not_10_out, not_11_out);
  and and_9 (and_9_out, D1, not_12_out);
  and and_10 (and_10_out, not_13_out, D3, D4);
  and and_11 (and_11_out, D2, not_14_out);
  and and_12 (and_12_out, D2, not_15_out);
  or or_1 (Q1, and_1_out, and_2_out, and_3_out, and_4_out, and_5_out);
  or or_2 (Q2, and_6_out, and_7_out, and_8_out, and_9_out);
  or or_3 (Q3, and_10_out, and_11_out, and_12_out);

  assign Q0 = 1'b0;
  assign Q4 = D3;
endmodule

module MULTIPLEXADOR (
  input  [3:0] in_1,
  input  in_2,
  output [3:0] out_3
);

  wire not_1_out;

  not not_1 (not_1_out, in_2);
  and and_1 (out_3[0], ~not_1_out, in_1[0]);  // AND_Gate
  and and_2 (out_3[1], ~not_1_out, in_1[1]);  // AND_Gate
  and and_3 (out_3[2], ~not_1_out, in_1[2]);  // AND_Gate
  and and_4 (out_3[3], ~not_1_out, in_1[3]);  // AND_Gate
endmodule

module PONTO (
  input  CLK,
  input  CLEAR,
  input  ENABLE,
  output [3:0] out_4
);

  wire [4:0] somador_1_out_3;

  D_Flip_Flop d_ff_1 (.clk(CLK), .D(somador_1_out_3[3]), .Q(out_4[3]), .en(ENABLE), .reset(CLEAR));  // open: Qn, preset
  D_Flip_Flop d_ff_2 (.clk(CLK), .D(somador_1_out_3[2]), .Q(out_4[2]), .en(ENABLE), .reset(CLEAR));  // open: Qn, preset
  SOMADOR somador_1 (.in_1(out_4), .in_2(4'b0001), .out_3(somador_1_out_3));  // open: out_4
  D_Flip_Flop d_ff_3 (.clk(CLK), .D(somador_1_out_3[1]), .Q(out_4[1]), .en(ENABLE), .reset(CLEAR));  // open: Qn, preset
  Hex_Digit_Display hex_digit_display_1 (.value(out_4));  // open: dp
  D_Flip_Flop d_ff_4 (.clk(CLK), .D(somador_1_out_3[0]), .Q(out_4[0]), .en(ENABLE), .reset(CLEAR));  // open: Qn, preset
endmodule

module MULTIPLEXADOR_SML (
  input  JOGADOR,
  input  in_2,
  output out_3,
  output out_4
);

  and and_1 (out_3, JOGADOR, in_2);
  and and_2 (out_4, ~JOGADOR, in_2);  // AND_Gate
endmodule

module TIMER_OU (
  input  in_1,
  input  in_2,
  input  in_3,
  input  in_4,
  input  in_5,
  input  in_6,
  input  in_7,
  input  in_8,
  output out_9,
  output out_10,
  output out_11,
  output out_12
);

  or or_1 (out_9, in_1, in_2);
  or or_2 (out_10, in_3, in_4);
  or or_3 (out_11, in_5, in_6);
  or or_4 (out_12, in_7, in_8);
endmodule

module INVERTER (
  input  Q0,
  input  Q1,
  output D0
);

  wire and_1_out, and_2_out, not_1_out, not_2_out;

  not not_1 (not_1_out, Q0);
  not not_2 (not_2_out, Q1);
  and and_1 (and_1_out, not_1_out, Q1);
  and and_2 (and_2_out, Q0, not_2_out);
  or or_1 (D0, and_1_out, and_2_out);
endmodule

module MULTIPLEX (
  input  CLK,
  input  CONF,
  output OUT
);

  wire not_1_out;

  not not_1 (not_1_out, CONF);
  and and_1 (OUT, CLK, not_1_out);
endmodule

module A (
  input  D0,
  input  D1,
  input  D2,
  input  D3,
  output Q0,
  output Q1,
  output Q2,
  output Q3,
  output SS,
  output zz
);

  wire and_1_out, and_2_out, and_3_out, and_4_out, and_5_out, and_6_out, and_8_out, and_9_out, not_1_out,
       not_2_out, not_3_out, not_4_out, not_5_out, not_6_out, not_7_out, not_8_out, not_10_out, not_11_out,
       not_12_out, not_13_out;

  not not_1 (not_1_out, D0);
  not not_2 (not_2_out, D1);
  not not_3 (not_3_out, D2);
  not not_4 (not_4_out, D3);
  and and_1 (and_1_out, D1, D3);
  and and_2 (and_2_out, D1, D2);
  and and_3 (and_3_out, D0, not_5_out);
  not not_5 (not_5_out, D3);
  and and_4 (and_4_out, D2, D3);
  and and_5 (and_5_out, D1, not_6_out, not_7_out);
  not not_6 (not_6_out, D2);
  not not_7 (not_7_out, D3);
  and and_6 (and_6_out, D0, not_8_out);
  not not_8 (not_8_out, D3);
  not not_9 (Q3, D3);
  and and_7 (SS, D0, D3);
  not not_10 (not_10_out, D0);
  not not_11 (not_11_out, D1);
  not not_12 (not_12_out, D2);
  not not_13 (not_13_out, D3);
  and and_8 (and_8_out, not_1_out, not_2_out, not_3_out, not_4_out);
  or or_1 (Q0, and_8_out, and_9_out);
  and and_9 (and_9_out, D0, D3);
  or or_2 (Q1, and_1_out, and_2_out, and_3_out);
  or or_3 (Q2, and_4_out, and_5_out, and_6_out);
  and and_10 (zz, not_10_out, not_11_out, not_12_out, not_13_out);
endmodule

module B (
  input  D0,
  input  D1,
  input  D2,
  input  D3,
  output Q0,
  output Q1,
  output Q2,
  output Q3,
  output SS,
  output zz
);

  wire and_1_out, and_2_out, and_3_out, and_4_out, and_5_out, not_1_out, not_2_out, not_3_out, not_4_out,
       not_5_out, not_6_out, not_8_out, not_9_out, not_10_out, not_11_out;

  not not_1 (not_1_out, D1);
  and and_1 (and_1_out, not_1_out, not_2_out, not_3_out);
  not not_2 (not_2_out, D2);
  not not_3 (not_3_out, D3);
  and and_2 (and_2_out, D1, D3);
  and and_3 (and_3_out, D2, D3);
  and and_4 (and_4_out, D1, not_4_out, not_5_out);
  not not_4 (not_4_out, D2);
  not not_5 (not_5_out, D3);
  and and_5 (and_5_out, D0, not_6_out);
  not not_6 (not_6_out, D3);
  not not_7 (Q3, D3);
  and and_6 (SS, D1, D3);
  not not_8 (not_8_out, D0);
  not not_9 (not_9_out, D1);
  not not_10 (not_10_out, D2);
  not not_11 (not_11_out, D3);
  or or_1 (Q1, and_1_out, and_2_out);
  or or_2 (Q2, and_3_out, and_4_out, and_5_out);
  and and_7 (zz, not_8_out, not_9_out, not_10_out, not_11_out);

  assign Q0 = 1'b0;
endmodule

module COMPARADOR_5B (
  input  [4:0] CHUTE,
  input  in_2,
  input  [4:0] in_3,
  output [2:0] out_4
);

  wire _0_2_out, _0_out, _1_2_out, _1_out, _2_2_out, _2_out, _3_2_out, _3_out, _4_2_out, _4_out, MAIOR_out,
       MENOR_out, xor_1_out, xor_2_out;

  xnor _0 (_0_out, in_3[0], CHUTE[0]);
  xnor _1 (_1_out, in_3[1], CHUTE[1]);
  xnor _2 (_2_out, in_3[2], CHUTE[2]);
  xnor _3 (_3_out, in_3[3], CHUTE[3]);
  xnor _4 (_4_out, in_3[4], CHUTE[4]);
  and IGUAL (out_4[1], _0_out, _1_out, _2_out, _3_out, _4_out);
  and _0_2 (_0_2_out, CHUTE[0], _1_out, _2_out, _3_out, ~in_3[0], _4_out);  // AND_Gate
  and _1_2 (_1_2_out, CHUTE[1], ~in_3[1], _4_out, _2_out, _3_out);  // AND_Gate
  and _2_2 (_2_2_out, CHUTE[2], ~in_3[2], _3_out, _4_out);  // AND_Gate
  and _3_2 (_3_2_out, CHUTE[3], ~in_3[3], _4_out);  // AND_Gate
  and _4_2 (_4_2_out, CHUTE[4], ~in_3[4]);  // AND_Gate
  or MAIOR (MAIOR_out, _0_2_out, _1_2_out, _4_2_out, _2_2_out, _3_2_out);
  nor MENOR (MENOR_out, out_4[1], MAIOR_out);
  ExactlyOne xor_1 (.out(xor_1_out), .in0(in_2), .in1(out_4[1]), .in2(MENOR_out));
  ExactlyOne xor_2 (.out(xor_2_out), .in0(in_2), .in1(out_4[1]), .in2(MAIOR_out));
  and and_1 (out_4[0], ~out_4[1], xor_1_out);  // AND_Gate
  and and_2 (out_4[2], ~out_4[1], xor_2_out);  // AND_Gate
endmodule

module NEGA (
  input  D0,
  input  D1,
  input  D2,
  input  D3,
  input  D4,
  output Q0,
  output Q1,
  output Q2,
  output Q3
);

  wire and_1_out, and_2_out, and_3_out, and_4_out, and_5_out, and_6_out, and_7_out, and_8_out, and_9_out,
       and_10_out, not_1_out, not_2_out, not_3_out, not_4_out, not_5_out, not_6_out, not_7_out, not_8_out;

  and and_1 (and_1_out, D3, D4);
  and and_2 (and_2_out, D2, D4);
  and and_3 (and_3_out, D1, D4);
  not not_1 (not_1_out, D1);
  not not_2 (not_2_out, D1);
  not not_3 (not_3_out, D2);
  not not_4 (not_4_out, D3);
  not not_5 (not_5_out, D4);
  not not_6 (not_6_out, D2);
  not not_7 (not_7_out, D3);
  not not_8 (not_8_out, D4);
  or or_1 (Q0, and_1_out, and_2_out, and_3_out, D0);
  and and_4 (and_4_out, not_1_out, D3, D4);
  and and_5 (and_5_out, not_2_out, D2, D4);
  and and_6 (and_6_out, D1, not_3_out, not_4_out);
  and and_7 (and_7_out, D1, not_5_out);
  and and_8 (and_8_out, not_6_out, D3, D4);
  and and_9 (and_9_out, D2, not_7_out);
  and and_10 (and_10_out, D2, not_8_out);
  or or_2 (Q1, and_4_out, and_5_out, and_6_out, and_7_out);
  or or_3 (Q2, and_8_out, and_9_out, and_10_out);

  assign Q3 = D3;
endmodule

module VISOR_NEGADO (
  input  D0,
  input  D1,
  input  D2,
  input  D3,
  output Q0,
  output Q1,
  output Q2,
  output Q3
);

  wire and_1_out, and_2_out, and_3_out, and_4_out, and_5_out, and_6_out, and_7_out, not_1_out, not_2_out,
       not_3_out, not_4_out, not_5_out, not_6_out, not_7_out, not_8_out, not_9_out, not_10_out, not_11_out;

  not not_1 (not_1_out, D1);
  not not_2 (not_2_out, D2);
  not not_3 (not_3_out, D3);
  not not_4 (not_4_out, D0);
  and and_1 (and_1_out, not_4_out, D1);
  and and_2 (and_2_out, D1, not_5_out, not_6_out);
  not not_5 (not_5_out, D2);
  not not_6 (not_6_out, D3);
  and and_3 (and_3_out, D0, not_7_out, D3);
  not not_7 (not_7_out, D1);
  and and_4 (and_4_out, D0, not_8_out, D2);
  not not_8 (not_8_out, D1);
  not not_9 (not_9_out, D0);
  and and_5 (and_5_out, not_9_out, D2);
  and and_6 (and_6_out, D2, not_10_out);
  not not_10 (not_10_out, D3);
  and and_7 (and_7_out, D0, not_11_out, D3);
  not not_11 (not_11_out, D2);
  and and_8 (Q0, D0, not_1_out, not_2_out, not_3_out);
  or or_1 (Q1, and_1_out, and_2_out, and_3_out, and_4_out);
  or or_2 (Q2, and_5_out, and_6_out, and_7_out);

  assign Q3 = D3;
endmodule

module VERIFICADOR (
  input  PROX,
  input  CLEAR,
  input  ENABLE,
  output out_4,
  output out_5,
  output out_6,
  output out_7
);

  wire d_ff_1_q, d_ff_2_q, ver1_1_q0, ver1_1_q1;

  D_Flip_Flop d_ff_1 (.clk(PROX), .D(ver1_1_q1), .Q(d_ff_1_q), .en(ENABLE), .reset(CLEAR));  // open: Qn, preset
  VER1 ver1_1 (.D0(d_ff_2_q), .D1(d_ff_1_q), .Q0(ver1_1_q0), .Q1(ver1_1_q1));
  D_Flip_Flop d_ff_2 (.clk(PROX), .D(ver1_1_q0), .Q(d_ff_2_q), .en(ENABLE), .reset(CLEAR));  // open: Qn, preset
  and and_1 (out_4, ~d_ff_2_q, ~d_ff_1_q);  // AND_Gate
  and and_2 (out_5, ~d_ff_2_q, d_ff_1_q);  // AND_Gate
  and and_3 (out_6, d_ff_2_q, ~d_ff_1_q);  // AND_Gate
  and and_4 (out_7, d_ff_2_q, d_ff_1_q);
endmodule

module VER1 (
  input  D0,
  input  D1,
  output Q0,
  output Q1
);

  wire and_1_out, and_2_out, not_1_out, not_2_out;

  not not_1 (not_1_out, D0);
  not not_2 (not_2_out, D1);
  not not_3 (Q1, D1);
  and and_1 (and_1_out, not_1_out, D1);
  and and_2 (and_2_out, D0, not_2_out);
  or or_1 (Q0, and_1_out, and_2_out);
endmodule

module TROCA (
  input  in_1,
  output out_2
);

  wire not_1_out;

  not not_1 (not_1_out, out_2);
  D_Flip_Flop d_ff_1 (.clk(in_1), .D(not_1_out), .Q(out_2));  // open: Qn, preset, en, reset
endmodule
